# Fritzing sketch OctoRemoteWiring (saved by Fritzing 1.0.1rc)
breadboards: 1

parts:
  Part1 = Arduino Nano (Rev3.0)
  Part2 = LED Tactile Button Breakout v10 [part_number=BOB-10467]
  Part4 = NRF24L01

nets:
  N1: Part1.D9, Part2.3
  N2: Part1.D10, Part2.2
  N3: Part1.D11/MOSI, Part4.MOSI
  N4: Part1.D12/MISO, Part4.MISO
  GND: Part1.GND, Part2.1, Part2.4, Part4.GND
  N5: Part1.A1, Part4.IRQ
  N6: Part1.A0, Part4.CSN, Part4.CE
  3V3: Part1.3V3, Part4.VCC
  N7: Part1.D13/SCK, Part4.SCK

notes:
  Version 0.1
